# Fritzing sketch LEDPillar (saved by Fritzing 0.9.3b)

parts:
  Part1 = Arduino Nano (Rev3.0)
  NEOPIXEL1 = Neopixel Strip -- Black (30/m)
  S1 = Round Pushbutton
  S3 = Round Pushbutton
  S4 = Round Pushbutton
  Part2 = LED Matrix - Serial Interface - Red/Green/Blue
  Part3 = LED Matrix - Serial Interface - Red/Green/Blue
  Part4 = LED Matrix - Serial Interface - Red/Green/Blue
  Part5 = LED Matrix - Serial Interface - Red/Green/Blue

nets:
  GND: Part1.GND, NEOPIXEL1.GND, S1.leg1, S3.leg1, S4.leg1, Part2.GND
  N1: Part1.D2, S3.leg0
  N2: Part1.D3, S1.leg0
  N3: Part1.D4, S4.leg0
  N4: Part1.D10, Part2.CS
  N5: Part1.D11/MOSI, Part2.MOSI
  N6: Part1.D12/MISO, NEOPIXEL1.Din
  5V: Part1.5V, NEOPIXEL1.+5V, Part2.VCC
  N7: Part1.D13/SCK, Part2.SCK
  GND_2: Part3.GND, Part4.GND, Part5.GND

custom parts:
  Neopixel Strip -- Black (30/m): These NeoPixel strips have 30 digitally-addressable pixel LEDs per meter and are very affordable and are only 12.5 mm wide, 10 mm if you remove the strip from the casing.
